// Logisim project cpu.circ as structural Verilog: 10 circuits, main circuit main
// IRQ
module main (
  input  IRQ,
  output RD,
  output WR,
  output [17:0] A
);

  wire alu_1_cf_af_out, alu_1_sf_out, alu_1_vf_out, alu_1_zf_out, flags_1_cf_af_out, mid_1_p7, mid_1_p8,
       mid_1_p9, mid_1_p10, mid_1_p11, mid_1_p12, mid_1_p13, mid_1_p15, mid_1_p17, mid_1_p19, mid_1_p20,
       mid_1_p21, undriven, undriven_2, undriven_4, undriven_5, undriven_8, undriven_9;
  wire [1:0] mid_1_p6, undriven_3, undriven_6, undriven_7;
  wire [2:0] mid_1_p14, mid_1_p16;
  wire [7:0] A_t, alu_1_c, B, grf_1_a, MD, mid_1_p1, mid_1_p2, mid_1_p3, mid_1_p18, srf_1_iph, srf_1_sph,
       srf_1_tmph, SS, X, Y;
  wire [15:0] inc_1_inc_res, IP, SP, srf_1_inc_in, TMP;

  // K8_18_Microcode_ROM k8_18_microcode_rom_1: pin names not known
  CU cu_1 ();  // open: psw, fs, cnd, nmip, cnd_nmip, md, nxt, out_9, clk
  ROM #(.dataWidth(32)) rom_1 ();  // open: addr, data, sel
  // MID mid_1: pin names not known; wires that end beside it: mid_1_p1, mid_1_p2, mid_1_p3, RD, WR, mid_1_p6, mid_1_p7, mid_1_p8, mid_1_p9, mid_1_p10, mid_1_p11, mid_1_p12, mid_1_p13, mid_1_p14, mid_1_p15, mid_1_p16, mid_1_p17, mid_1_p18, mid_1_p19, mid_1_p20, mid_1_p21
  ADDR addr_1 (
    .ss(SS), .iph(srf_1_iph), .sph(srf_1_sph), .tmph(srf_1_tmph), .y(Y), .c(alu_1_c), .adr(A), .hs(mid_1_p6),
    .he(mid_1_p7), .cs(mid_1_p8), .ds(mid_1_p9));
  SRF srf_1 (
    .b(mid_1_p1), .c(alu_1_c), .swe(mid_1_p15), .sws(mid_1_p16), .iip(mid_1_p11), .DEBUG_ip(IP),
    .isp(mid_1_p12), .DEBUG_sp(SP), .DEBUG_tmp(TMP), .rd(RD), .md_out(mid_1_p3), .DEBUG_md(MD),
    .srs(mid_1_p14), .soe(mid_1_p13), .clk(undriven), .inc_res(inc_1_inc_res), .inc_in(srf_1_inc_in),
    .md_in(mid_1_p2), .ss_out(SS), .iph(srf_1_iph), .sph(srf_1_sph), .tmph(srf_1_tmph));
  INC inc_1 (.inc_in(srf_1_inc_in), .dec(mid_1_p10), .inc_res(inc_1_inc_res));
  FLAGS flags_1 (
    .cf_af_in(alu_1_cf_af_out), .zf_in(alu_1_zf_out), .sf_in(alu_1_sf_out), .vf_in(alu_1_vf_out), .irq(IRQ),
    .c(alu_1_c), .fws(mid_1_p17), .fs(mid_1_p18), .sa(mid_1_p20), .ec(mid_1_p21),
    .cf_af_out(flags_1_cf_af_out), .out(mid_1_p1), .clk(undriven), .feo(mid_1_p19));
  ALU alu_1 (
    .op(undriven_3), .cf_af_in(flags_1_cf_af_out), .a(grf_1_a), .b(mid_1_p1), .inv(undriven_2),
    .rl(undriven_4), .rr(undriven_5), .vf_out(alu_1_vf_out), .sf_out(alu_1_sf_out),
    .cf_af_out(alu_1_cf_af_out), .c(alu_1_c), .zf_out(alu_1_zf_out));
  GRF grf_1 (
    .y_reg(Y), .a(grf_1_a), .c(alu_1_c), .DEBUG_B(B), .DEBUG_A(A_t), .DEBUG_X(X), .goe(undriven_8),
    .grs(undriven_6), .gwe(undriven_9), .gws(undriven_7), .clk(undriven));
endmodule

module GRF (
  input  goe,
  input  [1:0] grs,
  input  gwe,
  input  [1:0] gws,
  input  [7:0] c,
  input  clk,
  output [7:0] y_reg,
  output [7:0] DEBUG_B,
  output [7:0] DEBUG_A,
  output [7:0] a,
  output [7:0] DEBUG_X
);

  wire decoder_1_out0, decoder_1_out1, decoder_1_out2, decoder_1_out3;

  Multiplexer #(.select(2), .width(8)) multiplexer_1 (
    .in0(DEBUG_B), .in1(DEBUG_A), .in2(y_reg), .in3(DEBUG_X), .out(a), .sel(grs), .en(goe));
  Decoder #(.select(2), .disabled(0)) decoder_1 (
    .out0(decoder_1_out0), .out1(decoder_1_out1), .out2(decoder_1_out2), .out3(decoder_1_out3), .sel(gws),
    .en(gwe));
  Register B (.D(c), .en(decoder_1_out0), .Q(DEBUG_B), .clk(clk));  // open: clr
  Register u_A (.D(c), .en(decoder_1_out1), .Q(DEBUG_A), .clk(clk));  // open: clr
  Register Y (.D(c), .en(decoder_1_out2), .Q(y_reg), .clk(clk));  // open: clr
  Register X (.D(c), .en(decoder_1_out3), .Q(DEBUG_X), .clk(clk));  // open: clr
endmodule

module SRF (
  input  [2:0] srs,
  input  soe,
  input  swe,
  input  [2:0] sws,
  input  iip,
  input  isp,
  input  rd,
  input  [7:0] c,
  input  clk,
  input  [15:0] inc_res,
  input  [7:0] md_in,
  output [15:0] DEBUG_ip,
  output [15:0] DEBUG_sp,
  output [15:0] DEBUG_tmp,
  output [7:0] DEBUG_md,
  output [7:0] md_out,
  output [7:0] b,
  output [7:0] iph,
  output [7:0] sph,
  output [15:0] inc_in,
  output [7:0] tmph,
  output [7:0] ss_out
);

  wire decoder_1_out0, decoder_1_out1, decoder_1_out2, decoder_1_out3, decoder_1_out4, decoder_1_out5,
       decoder_1_out6, decoder_1_out7, hls_1_wh_out, hls_1_wl_out, hls_2_wh_out, hls_2_wl_out, or_1_out;
  wire [7:0] hls_1_high, hls_1_low, hls_2_high, hls_2_low, multiplexer_1_out;

  Decoder #(.select(3), .disabled(0)) decoder_1 (
    .out0(decoder_1_out0), .out1(decoder_1_out1), .out2(decoder_1_out2), .out3(decoder_1_out3),
    .out4(decoder_1_out4), .out5(decoder_1_out5), .out6(decoder_1_out6), .out7(decoder_1_out7), .sel(sws),
    .en(swe));
  Register IPL (.D(hls_1_low), .en(hls_1_wl_out), .Q(DEBUG_ip[7:0]), .clk(clk));  // open: clr
  HLS hls_1 (
    .inc(iip), .wl(decoder_1_out0), .inc_res(inc_res), .c(c), .wh(decoder_1_out1), .low(hls_1_low),
    .wl_out(hls_1_wl_out), .high(hls_1_high), .wh_out(hls_1_wh_out));
  Register u_IPH (.D(hls_1_high), .en(hls_1_wh_out), .Q(DEBUG_ip[15:8]), .clk(clk));  // open: clr
  assign inc_in = iip ? DEBUG_ip : 16'bz;  // Controlled_Buffer controlled_buffer_1
  Register SPL (.D(hls_2_low), .en(hls_2_wl_out), .Q(DEBUG_sp[7:0]), .clk(clk));  // open: clr
  Register u_SPH (.D(hls_2_high), .en(hls_2_wh_out), .Q(DEBUG_sp[15:8]), .clk(clk));  // open: clr
  HLS hls_2 (
    .inc(isp), .wl(decoder_1_out2), .inc_res(inc_res), .c(c), .wh(decoder_1_out3), .low(hls_2_low),
    .wl_out(hls_2_wl_out), .high(hls_2_high), .wh_out(hls_2_wh_out));
  assign inc_in = isp ? DEBUG_sp : 16'bz;  // Controlled_Buffer controlled_buffer_2
  Register TMPL (.D(c), .en(decoder_1_out4), .Q(DEBUG_tmp[7:0]), .clk(clk));  // open: clr
  Register u_TMPH (.D(c), .en(decoder_1_out5), .Q(DEBUG_tmp[15:8]), .clk(clk));  // open: clr
  Register MD (.D(multiplexer_1_out), .en(or_1_out), .Q(DEBUG_md), .clk(clk));  // open: clr
  or or_1 (or_1_out, rd, decoder_1_out6);
  Multiplexer #(.width(8)) multiplexer_1 (.in0(c), .in1(md_in), .out(multiplexer_1_out), .sel(rd));  // open: en
  Register SS (.D(c), .en(decoder_1_out7), .Q(ss_out), .clk(clk));  // open: clr
  Multiplexer #(.select(3), .width(8)) multiplexer_2 (
    .in0(DEBUG_ip[7:0]), .in1(DEBUG_ip[15:8]), .in2(DEBUG_sp[7:0]), .in3(DEBUG_sp[15:8]),
    .in4(DEBUG_tmp[7:0]), .in5(DEBUG_tmp[15:8]), .in6(DEBUG_md), .in7(ss_out), .out(b), .sel(srs), .en(soe));

  assign iph = DEBUG_ip[15:8];
  assign md_out = DEBUG_md;
  assign sph = DEBUG_sp[15:8];
  assign tmph = DEBUG_tmp[15:8];
endmodule

module HLS (
  input  inc,
  input  wl,
  input  [15:0] inc_res,
  input  [7:0] c,
  input  wh,
  output [7:0] low,
  output wl_out,
  output [7:0] high,
  output wh_out
);

  Multiplexer #(.width(8)) multiplexer_1 (.in0(c), .in1(inc_res[7:0]), .out(low), .sel(inc));  // open: en
  or or_1 (wl_out, inc, wl);
  Multiplexer #(.width(8)) multiplexer_2 (.in0(c), .in1(inc_res[15:8]), .out(high), .sel(inc));  // open: en
  or or_2 (wh_out, inc, wh);
endmodule

module INC (
  input  [15:0] inc_in,
  input  dec,
  output [15:0] inc_res
);

  wire [15:0] xor_1_out;

  assign xor_1_out = 16'h1 ^ {16{dec}};  // XOR_Gate xor_1, 16 bits wide
  Adder #(.width(16)) adder_1 (.a(inc_in), .b(xor_1_out), .out(inc_res), .cin(dec));  // open: cout
endmodule

module MID (
  input  [31:0] mi1,
  input  [23:0] mi1_2,
  output goe,
  output gwe,
  output [1:0] gws,
  output [1:0] grs,
  output rr,
  output rl,
  output [1:0] op,
  output inv,
  output ec,
  output sa,
  output feo,
  output [7:0] fs,
  output fws,
  output [2:0] sws,
  output swe,
  output [2:0] srs,
  output soe,
  output isp,
  output iip,
  output dec,
  output ds,
  output cs,
  output he,
  output [1:0] hs,
  output wr,
  output cnd,
  output rd,
  output nxt,
  output [11:0] nmip,
  output [11:0] cnd_nmip
);

  assign cnd_nmip = mi1[11:0] & ~{12{mi1_2[7]}};  // AND_Gate and_1, 12 bits wide

  assign cnd = mi1_2[8];
  assign cs = mi1_2[3];
  assign dec = mi1_2[1];
  assign ds = mi1_2[2];
  assign ec = cnd_nmip[11];
  assign feo = mi1[13];
  assign fs = mi1[21:14];
  assign fws = mi1[22];
  assign goe = cnd_nmip[0];
  assign grs = cnd_nmip[5:4];
  assign gwe = cnd_nmip[1];
  assign gws = cnd_nmip[3:2];
  assign he = mi1_2[4];
  assign hs = mi1_2[6:5];
  assign iip = mi1_2[0];
  assign inv = cnd_nmip[10];
  assign isp = mi1[31];
  assign nmip = mi1_2[23:12];
  assign nxt = mi1_2[10];
  assign op = cnd_nmip[9:8];
  assign rd = mi1_2[9];
  assign rl = cnd_nmip[7];
  assign rr = cnd_nmip[6];
  assign sa = mi1[12];
  assign soe = mi1[30];
  assign srs = mi1[29:27];
  assign swe = mi1[26];
  assign sws = mi1[25:23];
  assign wr = mi1_2[7];
endmodule

module ALU (
  input  [1:0] op,
  input  cf_af_in,
  input  [7:0] a,
  input  [7:0] b,
  input  inv,
  input  rl,
  input  rr,
  output vf_out,
  output sf_out,
  output cf_af_out,
  output [7:0] c,
  output zf_out
);

  wire adder_1_cout, nor_1_out, or_1_out, xor_2_out, xor_3_out;
  wire [7:0] adder_1_out, and_1_out, multiplexer_1_out, or_2_out, xor_1_out, xor_4_out;

  assign xor_1_out = b ^ {8{inv}};  // XOR_Gate xor_1, 8 bits wide
  or or_1 (or_1_out, a[7], xor_1_out[7]);
  xor xor_2 (xor_2_out, inv, cf_af_in);
  Adder adder_1 (.a(a), .b(xor_1_out), .out(adder_1_out), .cin(xor_2_out), .cout(adder_1_cout));
  xor xor_3 (xor_3_out, adder_1_cout, inv);
  assign or_2_out = xor_1_out | a;  // OR_Gate or_2, 8 bits wide
  assign and_1_out = a & xor_1_out;  // AND_Gate and_1, 8 bits wide
  assign xor_4_out = a ^ xor_1_out;  // XOR_Gate xor_4, 8 bits wide
  Multiplexer #(.select(2), .width(8)) multiplexer_1 (
    .in0(adder_1_out), .in1(or_2_out), .in2(and_1_out), .in3(xor_4_out), .out(multiplexer_1_out), .sel(op));  // open: en
  assign cf_af_out = nor_1_out ? xor_3_out : 1'bz;  // Controlled_Buffer controlled_buffer_1
  assign cf_af_out = rr ? multiplexer_1_out[0] : 1'bz;  // Controlled_Buffer controlled_buffer_2
  assign cf_af_out = rl ? multiplexer_1_out[7] : 1'bz;  // Controlled_Buffer controlled_buffer_3
  assign c = rl ? {multiplexer_1_out[6:0], multiplexer_1_out[7]} : 8'bz;  // Controlled_Buffer controlled_buffer_4
  assign c = nor_1_out ? multiplexer_1_out : 8'bz;  // Controlled_Buffer controlled_buffer_5
  nor nor_1 (nor_1_out, rl, rr);
  assign c = rr ? {multiplexer_1_out[0], multiplexer_1_out[7:1]} : 8'bz;  // Controlled_Buffer controlled_buffer_6
  xor xor_5 (vf_out, or_1_out, c[7]);
  nor nor_2 (zf_out, c[0], c[1], c[2], c[3], c[4], c[5], c[6], c[7]);

  assign sf_out = c[7];
endmodule

module FLAGS (
  input  [7:0] c,
  input  fws,
  input  [7:0] fs,
  input  sa,
  input  ec,
  input  feo,
  input  cf_af_in,
  input  zf_in,
  input  sf_in,
  input  vf_in,
  input  irq,
  input  clk,
  output cf_af_out,
  output [7:0] out
);

  wire and_1_out, and_2_out, and_3_out, and_4_out, and_5_out, and_6_out, and_7_out, and_8_out, and_9_out,
       multiplexer_1_out, multiplexer_2_out, multiplexer_3_out, multiplexer_4_out, multiplexer_5_out,
       or_1_out, or_2_out, or_3_out;
  wire [7:0] C_q;

  Multiplexer multiplexer_1 (.in0(c[0]), .in1(cf_af_in), .out(multiplexer_1_out), .sel(fws));  // open: en
  Multiplexer multiplexer_2 (.in0(c[1]), .in1(zf_in), .out(multiplexer_2_out), .sel(fws));  // open: en
  Multiplexer multiplexer_3 (.in0(c[2]), .in1(sf_in), .out(multiplexer_3_out), .sel(fws));  // open: en
  Multiplexer multiplexer_4 (.in0(c[3]), .in1(vf_in), .out(multiplexer_4_out), .sel(fws));  // open: en
  and and_1 (and_1_out, C_q[5], irq);
  or or_1 (or_1_out, c[4], multiplexer_1_out);
  or or_2 (or_2_out, fs[7], and_1_out);
  or or_3 (or_3_out, irq, c[7]);
  and and_2 (and_2_out, fs[0], clk);
  D_Flip_Flop u_C (.clk(and_2_out), .D(multiplexer_1_out), .Q(C_q[0]));  // open: Qn, preset, en, reset
  and and_3 (and_3_out, fs[1], clk);
  D_Flip_Flop Z (.clk(and_3_out), .D(multiplexer_2_out), .Q(C_q[1]));  // open: Qn, preset, en, reset
  and and_4 (and_4_out, fs[2], clk);
  D_Flip_Flop S (.clk(and_4_out), .D(multiplexer_3_out), .Q(C_q[2]));  // open: Qn, preset, en, reset
  and and_5 (and_5_out, fs[3], clk);
  D_Flip_Flop V (.clk(and_5_out), .D(multiplexer_4_out), .Q(C_q[3]));  // open: Qn, preset, en, reset
  D_Flip_Flop A (.clk(and_6_out), .D(or_1_out), .Q(C_q[4]));  // open: Qn, preset, en, reset
  and and_6 (and_6_out, fs[4], clk);
  D_Flip_Flop E (.clk(and_7_out), .D(c[5]), .Q(C_q[5]));  // open: Qn, preset, en, reset
  and and_7 (and_7_out, fs[5], clk);
  D_Flip_Flop P (.clk(and_8_out), .D(c[6]), .Q(C_q[6]));  // open: Qn, preset, en, reset
  and and_8 (and_8_out, fs[6], clk);
  and and_9 (and_9_out, or_2_out, clk);
  D_Flip_Flop I (.clk(and_9_out), .D(or_3_out), .Q(C_q[7]));  // open: Qn, preset, en, reset
  and and_10 (cf_af_out, ec, multiplexer_5_out);
  Multiplexer multiplexer_5 (.in0(C_q[0]), .in1(C_q[4]), .out(multiplexer_5_out), .sel(sa));  // open: en
  assign out = feo ? C_q : 8'bz;  // Controlled_Buffer controlled_buffer_1
endmodule

module CU (
  input  [7:0] psw,
  input  [7:0] fs,
  input  cnd,
  input  [11:0] nmip,
  input  [11:0] cnd_nmip,
  input  [7:0] md,
  input  nxt,
  input  clk,
  output [11:0] out_9
);

  wire and_2_out, or_1_out;
  wire [7:0] and_1_out;
  wire [11:0] multiplexer_1_out, multiplexer_2_out, not_1_out, register_1_q;

  assign and_1_out = psw & fs;  // AND_Gate and_1, 8 bits wide
  or or_1 (or_1_out, and_1_out[0], and_1_out[1], and_1_out[2], and_1_out[3], and_1_out[4], and_1_out[5], and_1_out[6], and_1_out[7]);
  and and_2 (and_2_out, cnd, or_1_out);
  Multiplexer #(.width(12)) multiplexer_1 (
    .in0(nmip), .in1(cnd_nmip), .out(multiplexer_1_out), .sel(and_2_out));  // open: en
  Multiplexer #(.width(12)) multiplexer_2 (
    .in0(multiplexer_1_out), .in1({psw[6], 3'b000, md}), .out(multiplexer_2_out), .sel(nxt));  // open: en
  assign not_1_out = ~multiplexer_2_out;  // NOT_Gate not_1, 12 bits wide
  Register #(.width(12)) register_1 (.D(not_1_out), .Q(register_1_q), .clk(clk));  // open: en, clr
  assign out_9 = ~register_1_q;  // NOT_Gate not_2, 12 bits wide

  // Notes on the sheet:
  //   P flag
endmodule

module ADDR (
  input  [1:0] hs,
  input  he,
  input  cs,
  input  ds,
  input  [7:0] ss,
  input  [7:0] iph,
  input  [7:0] sph,
  input  [7:0] tmph,
  input  [7:0] y,
  input  [7:0] c,
  output [17:0] adr
);

  wire [3:0] controlled_buffer_1_out;
  wire [7:6] multiplexer_1_out;

  Multiplexer #(.select(2), .width(8)) multiplexer_1 (
    .in0(iph), .in1(sph), .in2(tmph), .in3(y), .out({multiplexer_1_out, adr[13:8]}), .sel(hs), .en(he));
  Pull_Resistor pull_resistor_1 (.node({multiplexer_1_out, adr[13:8]}));
  assign controlled_buffer_1_out = ds ? ss[3:0] : 4'bz;  // Controlled_Buffer controlled_buffer_1
  assign controlled_buffer_1_out = cs ? ss[7:4] : 4'bz;  // Controlled_Buffer controlled_buffer_2
  Pull_Resistor pull_resistor_2 (.node(controlled_buffer_1_out));
  Adder #(.width(4)) adder_1 (
    .a(controlled_buffer_1_out), .b({multiplexer_1_out, 2'b00}), .out(adr[17:14]));  // open: cin, cout

  assign adr[7:0] = c;
endmodule
